// Logisim project cronometro.circ as structural Verilog: 5 circuits, main circuit main
module main (
  input  in_1,
  input  in_2,
  input  in_3,
  input  in_4
);

  wire and_1_out, and_2_out, and_3_out, and_4_out, and_5_out, and_6_out, and_7_out, clock_1_out;
  wire [1:0] _0_2_out_3;
  wire [2:0] _0___5_2_out_4, _0___5_out_4;
  wire [3:0] _0_9_2_out_5, _0_9_3_out_5, _0_9_out_5;

  and and_1 (and_1_out, _0_9_out_5[3], _0_9_out_5[0]);
  jk2 _0_2 (.in_1(and_1_out), .out_2(_0_2_out_3[1]), .out_3(_0_2_out_3[0]));
  Hex_Digit_Display hex_digit_display_1 (.value({{2{in_3}}, _0_2_out_3}));  // open: dp
  jk9 _0_9 (
    .in_1(and_3_out), .out_2(_0_9_out_5[3]), .out_3(_0_9_out_5[2]), .out_4(_0_9_out_5[1]),
    .out_5(_0_9_out_5[0]));
  and and_2 (and_2_out, _0_2_out_3[1], _0_9_out_5[1], _0_9_out_5[0]);
  Hex_Digit_Display hex_digit_display_2 (.value(_0_9_out_5));  // open: dp
  jk5 _0___5 (._0_1(and_4_out), .out_2(_0___5_out_4[2]), .out_3(_0___5_out_4[1]), .out_4(_0___5_out_4[0]));
  and and_3 (and_3_out, _0___5_out_4[2], _0___5_out_4[0]);
  Hex_Digit_Display hex_digit_display_3 (.value({in_2, _0___5_out_4}));  // open: dp
  jk9 _0_9_2 (
    .in_1(and_6_out), .out_2(_0_9_2_out_5[3]), .out_3(_0_9_2_out_5[2]), .out_4(_0_9_2_out_5[1]),
    .out_5(_0_9_2_out_5[0]));
  and and_4 (and_4_out, _0_9_2_out_5[3], _0_9_2_out_5[0]);
  Clock clock_1 (.out(clock_1_out));
  Hex_Digit_Display hex_digit_display_4 (.value(_0_9_2_out_5));  // open: dp
  and and_5 (and_5_out, clock_1_out, in_4);
  jk5 _0___5_2 (._0_1(and_7_out), .out_2(_0___5_2_out_4[2]), .out_3(_0___5_2_out_4[1]), .out_4(_0___5_2_out_4[0]));
  and and_6 (and_6_out, _0___5_2_out_4[2], _0___5_2_out_4[0]);
  Hex_Digit_Display hex_digit_display_5 (.value({in_1, _0___5_2_out_4}));  // open: dp
  jk9 _0_9_3 (
    .in_1(and_5_out), .out_2(_0_9_3_out_5[3]), .out_3(_0_9_3_out_5[2]), .out_4(_0_9_3_out_5[1]),
    .out_5(_0_9_3_out_5[0]));
  and and_7 (and_7_out, _0_9_3_out_5[3], _0_9_3_out_5[0]);
  Hex_Digit_Display hex_digit_display_6 (.value(_0_9_3_out_5));  // open: dp
endmodule

module jk9 (
  input  in_1,
  output out_2,
  output out_3,
  output out_4,
  output out_5
);

  wire A_qn, and_1_out, and_2_out, and_3_out;

  J_K_Flip_Flop #(.trigger("falling")) D (.J(1'b1), .clk(in_1), .K(1'b1), .Q(out_5));  // open: Qn, preset, en, reset
  and and_1 (and_1_out, out_5, A_qn);
  J_K_Flip_Flop #(.trigger("falling")) C (
    .J(and_1_out), .clk(in_1), .K(out_5), .Q(out_4));  // open: Qn, preset, en, reset
  and and_2 (and_2_out, out_5, out_4);
  J_K_Flip_Flop #(.trigger("falling")) B (
    .J(and_2_out), .clk(in_1), .K(and_2_out), .Q(out_3));  // open: Qn, preset, en, reset
  and and_3 (and_3_out, out_5, out_4, out_3);
  J_K_Flip_Flop #(.trigger("falling")) A (
    .J(and_3_out), .clk(in_1), .K(out_5), .Q(out_2), .Qn(A_qn));  // open: preset, en, reset
endmodule

module jk5 (
  input  _0_1,
  output out_2,
  output out_3,
  output out_4
);

  wire A_qn, and_1_out, and_2_out;

  J_K_Flip_Flop #(.trigger("falling")) C (.J(1'b1), .clk(_0_1), .K(1'b1), .Q(out_4));  // open: Qn, preset, en, reset
  and and_1 (and_1_out, A_qn, out_4);
  J_K_Flip_Flop #(.trigger("falling")) B (
    .J(and_1_out), .clk(_0_1), .K(out_4), .Q(out_3));  // open: Qn, preset, en, reset
  and and_2 (and_2_out, out_4, out_3);
  J_K_Flip_Flop #(.trigger("falling")) A (
    .J(and_2_out), .clk(_0_1), .K(out_4), .Q(out_2), .Qn(A_qn));  // open: preset, en, reset
endmodule

module jk3 (
  output out_1,
  output out_2
);

  wire clock_1_out;

  Clock clock_1 (.out(clock_1_out));
  J_K_Flip_Flop #(.trigger("falling")) B (
    .J(1'b1), .clk(clock_1_out), .K(1'b1), .Q(out_2));  // open: Qn, preset, en, reset
  J_K_Flip_Flop #(.trigger("falling")) A (
    .J(out_2), .clk(clock_1_out), .K(out_2), .Q(out_1));  // open: Qn, preset, en, reset
endmodule

module jk2 (
  input  in_1,
  output out_2,
  output out_3
);

  wire A_qn;

  J_K_Flip_Flop #(.trigger("falling")) B (.J(A_qn), .clk(in_1), .K(1'b1), .Q(out_3));  // open: Qn, preset, en, reset
  J_K_Flip_Flop #(.trigger("falling")) A (
    .J(out_3), .clk(in_1), .K(1'b1), .Q(out_2), .Qn(A_qn));  // open: preset, en, reset
endmodule
